// Digital circuit CPU.dig as structural Verilog
module CPU (
  input  [63:0] Databus_Manual_Input,
  input  CPU_Clock
);

  wire ADDRw, alu_1_equal_to, alu_1_greater_than, alu_1_lesser_than, CCclr, clock, Databus_Manual_Switch_out,
       DBout, driver_5_out, driverinvsel_3_out, ETf, GTf, IRw, LTf, Manual_Clock_Stepper_out,
       Manual_Stepping_out, not_1_out, PAinc, PAw, RAMr, RAMw, RAr, RAw, RBr, RBw, ROMr, SRr, SRw;
  wire [3:0] ALUop, Control_Counter_out;
  wire [19:0] Instruction_Register_q;
  wire [23:0] add_1_s, Address_Register_q, driverinvsel_2_out, Program_Address_Register_q;
  wire [43:0] Instruction_Register_q_2;
  wire [63:0] alu_1_x, bitextender_1_out, databus, RA, Register_B_q, Sum_Register_q;

  Register #(.Bits(64)) Register_A (.D(databus), .C(clock), .en(RAw), .Q(RA));
  Register #(.Bits(64)) Register_B (.D(databus), .C(clock), .en(RBw), .Q(Register_B_q));
  DipSwitch #(.dipDefault("true")) Manual_Stepping (.out(Manual_Stepping_out));
  Button Manual_Clock_Stepper (.out(Manual_Clock_Stepper_out));
  assign clock = Manual_Stepping_out ? Manual_Clock_Stepper_out : 1'bz;  // Driver driver_1
  assign clock = ~Manual_Stepping_out ? CPU_Clock : 1'bz;  // DriverInvSel driverinvsel_1
  assign databus = Databus_Manual_Switch_out ? Databus_Manual_Input : 64'bz;  // Driver driver_2
  DipSwitch Databus_Manual_Switch (.out(Databus_Manual_Switch_out));
  assign databus = RAr ? RA : 64'bz;  // Driver driver_3
  assign databus = RBr ? Register_B_q : 64'bz;  // Driver driver_4
  ALU alu_1 (
    .A(RA), .B(databus), .Operation(ALUop), .X(alu_1_x), .Lesser_Than(alu_1_lesser_than),
    .Equal_To(alu_1_equal_to), .Greater_Than(alu_1_greater_than));
  Register #(.Bits(24)) Address_Register (.D(databus[23:0]), .C(clock), .en(ADDRw), .Q(Address_Register_q));
  Register #(.Bits(64)) Sum_Register (.D(alu_1_x), .C(clock), .en(SRw), .Q(Sum_Register_q));
  assign driver_5_out = SRw ? clock : 1'bz;  // Driver driver_5
  D_FF LT_Reg (.D(alu_1_lesser_than), .C(driver_5_out), .Q(LTf));  // open: nQ
  D_FF ET_Reg (.D(alu_1_equal_to), .C(driver_5_out), .Q(ETf));  // open: nQ
  D_FF GT_Reg (.D(alu_1_greater_than), .C(driver_5_out), .Q(GTf));  // open: nQ
  assign databus = SRr ? Sum_Register_q : 64'bz;  // Driver driver_6
  RAMDualPort #(.AddrBits(24), .Bits(64)) ramdualport_1 (
    .A(Address_Register_q), .Din(databus), .str(RAMw), .C(clock), .ld(RAMr), .D(databus));
  Counter #(.Bits(4)) Control_Counter (.en(1'b1), .C(not_1_out), .clr(CCclr), .out(Control_Counter_out));  // open: ovf
  not not_1 (not_1_out, clock);
  Register #(.Bits(64)) Instruction_Register (
    .D(databus), .C(clock), .en(IRw), .Q({Instruction_Register_q_2, Instruction_Register_q}));
  assign driverinvsel_2_out = ~PAinc ? databus[23:0] : 24'bz;  // DriverInvSel driverinvsel_2
  assign driverinvsel_3_out = ~PAinc ? PAw : 1'bz;  // DriverInvSel driverinvsel_3
  assign driverinvsel_3_out = PAinc ? 1'b1 : 1'bz;  // Driver driver_7
  BitExtender #(.inputBits(44), .outputBits(64)) bitextender_1 (.in(Instruction_Register_q_2), .out(bitextender_1_out));
  assign driverinvsel_2_out = PAinc ? add_1_s : 24'bz;  // Driver driver_8
  assign databus = DBout ? bitextender_1_out : 64'bz;  // Driver driver_9
  Register #(.Bits(24)) Program_Address_Register (
    .D(driverinvsel_2_out), .C(clock), .en(driverinvsel_3_out), .Q(Program_Address_Register_q));
  Add #(.Bits(24)) add_1 (.a(Program_Address_Register_q), .b({24{1'b0}}), .c_i(1'b1), .s(add_1_s));  // open: c_o
  EEPROM #(.AddrBits(24), .Bits(19)) Logic_Table (
    .A({Instruction_Register_q, Control_Counter_out}), .CS(1'b1), .WE(1'b0), .OE(1'b1),
    .D({ALUop, DBout, RAw, RAr, RBw, RBr, SRw, SRr, ADDRw, RAMw, RAMr, PAw, CCclr, PAinc, ROMr, IRw}));
  EEPROM #(.AddrBits(24), .Bits(64)) eeprom_1 (
    .A(Program_Address_Register_q), .CS(1'b1), .WE(1'b0), .OE(ROMr), .D(databus));

  // Notes on the sheet:
  //   CPU_Clock: Hz: 2147483647
  //   Clock Control
  //   Manual Databus Control
  //   Register A
  //   Register B
  //   ALU & Sum Register
  //   RAM & Address Register
  //   Control Logic
  //   ROM & Program Address Register
  //   contents of Logic_Table (hex, n*v repeats v):
  //   7,8,14*0,7,200e,14*0,7,4080,1048,13*0,7,4080,2028,13*0,7,80e,14*0
  //   ,7,4080,448,13*0,7,4080,828,13*0,7,4080,4e,13*0,7,4080,220,2108
  //   ,12*0,7,4080,8220,2108,12*0,7,4080,10220,2108,12*0,7,4080,18220
  //   ,2108,12*0,3,4018
  //   contents of eeprom_1 (hex, n*v repeats v):
  //   7,1,8,20000c
endmodule
